# Fritzing sketch motorTransistor (saved by Fritzing 0.9.1b)
breadboards: 1

parts:
  Part1 = Arduino Uno (Rev3) - ICSP
  Q1 = TRANSISTOR_NPN [package=to-92]
  J1 = Power Jack [package=power_jack_smd]
  M1 = DC Motor
  D1 = Diode [package=diode-hv]

nets:
  N1: Part1.D2, Q1.B
  N2: Part1.GND, Q1.E, J1.GNDBREAK, D1.A
  N3: Q1.C, M1.pin_1, D1.C
  N4: J1.GND, M1.pin_2
