# Fritzing sketch parallel (saved by Fritzing 0.9.2b)
breadboards: 1

parts:
  Part1 = Arduino Uno (Rev3)
  LED1 = LED - 5mm [color="Red (633nm)" package="5 mm [THT]"]
  LED2 = LED - 5mm [color="Red (633nm)" package="5 mm [THT]"]
  R1 = Resistor [tolerance=±5% resistance=220 package="0402 [SMD]"]

nets:
  N1: Part1.5V, LED1.cathode, LED2.cathode
  N2: Part1.GND, R1.Pin_1
  N3: LED1.anode, LED2.anode, R1.Pin_0
