# Fritzing sketch series (saved by Fritzing 0.9.2b)
breadboards: 1

parts:
  Part1 = Arduino Uno (Rev3)
  LED2 = LED - 5mm [color="Red (633nm)" package="5 mm [THT]"]
  R1 = Resistor [tolerance=±5% resistance=220 package="0402 [SMD]"]
  LED1 = LED - 5mm [color="Red (633nm)" package="5 mm [THT]"]

nets:
  N1: Part1.5V, LED1.cathode
  N2: Part1.GND, R1.Pin_1
  N3: LED2.cathode, LED1.anode
  N4: LED2.anode, R1.Pin_0
