# Fritzing sketch switch (saved by Fritzing 0.9.0b)
breadboards: 1

parts:
  Part1 = Arduino Uno (Rev3)
  R1 = Resistor [tolerance=±5% resistance=10k package=THT]
  S2 = Square Pushbutton

nets:
  N1: Part1.D2, R1.Pin_0, S2.leg1
  N2: Part1.5V, S2.leg0
  N3: Part1.GND, R1.Pin_1
