# Fritzing sketch analog2wire (saved by Fritzing 0.9.0b)
breadboards: 1

parts:
  Part1 = Arduino Uno (Rev3)
  R1 = Resistor [tolerance=±5% resistance=10k package=THT]
  R2 = Photocell (LDR) [package=THT]

nets:
  N1: Part1.A0, R1.Pin_0, R2.pin_1
  N2: Part1.5V, R2.pin_0
  N3: Part1.GND, R1.Pin_1
